// Logisim project SAP3.circ as structural Verilog: 17 circuits, main circuit main
module main (
  input  in_1,
  input  in_2
);

  wire ALUOut, ByteSel, CF, clock_1_out, DisEn, HLT, ID, jump_1_jmp, MCReset, not_1_out, or_1_out, or_2_out,
       or_3_out, RAType, RegAccess, s_r_ff_1_q, SF, ZF;
  wire [0:0] and_1_out;
  wire [1:0] pull_resistor_2_node, pull_resistor_3_node, regcontroller_1_a, regcontroller_1_b,
       regcontroller_1_c, regcontroller_1_d, regcontroller_1_e, regcontroller_1_flag, regcontroller_1_h,
       regcontroller_1_inc_dec, regcontroller_1_l, regcontroller_1_mar, regcontroller_1_mdr,
       regcontroller_1_pc, regcontroller_1_stack, regcontroller_1_temp;
  wire [3:0] ALUSel, counter_1_q, display_1_hundreds, display_1_hundreds_2, display_1_ones, display_1_ones_2,
       display_1_tens, display_1_tens_2, display_1_tenthousands, display_1_tenthousands_2,
       display_1_thousands, display_1_thousands_2;
  wire [7:0] Accumulator_currentdata, alu_1_product, B_currentdata, C_currentdata, D_currentdata,
       E_currentdata, H_currentdata, L_currentdata, ram_1_dout, ramcontroller_1_ramwr, register_1_q,
       Temp_currentdata;
  wire [15:0] ramcontroller_1_addr, stack_1_currentstack;
  wire [23:8] MicroCode_data;

  or or_1 (or_1_out, HLT, in_1);
  S_R_Flip_Flop s_r_ff_1 (.S(HLT), .clk(or_1_out), .R(in_1), .Q(s_r_ff_1_q));  // open: Qn, preset, reset
  Clock clock_1 (.out(clock_1_out));
  _7_Segment_Display u_7_segment_display_1 (
    .g(display_1_tenthousands_2[2]), .f(display_1_tenthousands_2[1]), .a(display_1_tenthousands[0]),
    .b(display_1_tenthousands[1]), .e(display_1_tenthousands_2[0]), .d(display_1_tenthousands[3]),
    .c(display_1_tenthousands[2]));  // open: dp
  and and_1 (and_1_out[0], ~s_r_ff_1_q, clock_1_out, in_2);  // AND_Gate
  Pull_Resistor pull_resistor_1 (.node(pull_resistor_2_node[1]));
  Pull_Resistor pull_resistor_2 (.node(pull_resistor_2_node[0]));
  Register register_1 (.D(alu_1_product), .en(or_2_out), .Q(register_1_q), .clk(and_1_out[0]), .clr(in_1));
  or or_2 (or_2_out, pull_resistor_2_node[1], pull_resistor_2_node[0]);
  Counter #(.max('hf), .width(4)) counter_1 (
    .Q(counter_1_q), .clk(not_1_out), .clr(or_3_out));  // open: load, D, count, carry, up
  not not_1 (not_1_out, and_1_out[0]);
  or or_3 (or_3_out, in_1, MCReset);
  _7_Segment_Display u_7_segment_display_2 (
    .g(display_1_thousands_2[2]), .f(display_1_thousands_2[1]), .a(display_1_thousands[0]),
    .b(display_1_thousands[1]), .e(display_1_thousands_2[0]), .d(display_1_thousands[3]),
    .c(display_1_thousands[2]));  // open: dp
  RAMController ramcontroller_1 (
    .ByteSel(ByteSel), .MAR(alu_1_product), .MAREn(regcontroller_1_mar[1]), .MDREn(regcontroller_1_mdr[1]),
    .Clk_Clr({in_1, and_1_out[0]}), .Addr(ramcontroller_1_addr), .RAMWr(ramcontroller_1_ramwr));
  // Probe on MicroCode_data[11:8]
  Display display_1 (
    .Ones({display_1_ones_2, display_1_ones}), .Tens({display_1_tens_2, display_1_tens}),
    .Hundreds({display_1_hundreds_2, display_1_hundreds}),
    .Thousands({display_1_thousands_2, display_1_thousands}),
    .TenThousands({display_1_tenthousands_2, display_1_tenthousands}));  // open: UpperLoad, BusLine, LowerLoad, Clk_Clr, DisEn
  _7_Segment_Display u_7_segment_display_3 (
    .g(display_1_hundreds_2[2]), .f(display_1_hundreds_2[1]), .a(display_1_hundreds[0]),
    .b(display_1_hundreds[1]), .e(display_1_hundreds_2[0]), .d(display_1_hundreds[3]),
    .c(display_1_hundreds[2]));  // open: dp
  ALU alu_1 (
    .B(Temp_currentdata), .CFIn(CF), .ALUSel(ALUSel), .ALUOut(ALUOut), .Product(alu_1_product));  // open: A, CFOut
  RAM #(.addrWidth(16), .trigger("falling")) ram_1 (
    .addr(ramcontroller_1_addr), .we(pull_resistor_3_node[1]), .oe(1'b1), .clk(and_1_out[0]),
    .din(ramcontroller_1_ramwr), .dout(ram_1_dout));
  ROM #(.addrWidth(12), .dataWidth(24)) MicroCode (
    .addr({register_1_q, counter_1_q}),
    .data({MicroCode_data[23], DisEn, MCReset, HLT, MicroCode_data[19:17], ID, MicroCode_data[15:8], ByteSel, RegAccess, RAType, ALUOut, ALUSel}));
  // Probe on MicroCode_data[15:12]
  _7_Segment_Display u_7_segment_display_4 (
    .g(display_1_tens_2[2]), .f(display_1_tens_2[1]), .a(display_1_tens[0]), .b(display_1_tens[1]),
    .e(display_1_tens_2[0]), .d(display_1_tens[3]), .c(display_1_tens[2]));  // open: dp
  _7_Segment_Display u_7_segment_display_5 (
    .g(display_1_ones_2[2]), .f(display_1_ones_2[1]), .a(display_1_ones[0]), .b(display_1_ones[1]),
    .e(display_1_ones_2[0]), .d(display_1_ones[3]), .c(display_1_ones[2]));  // open: dp
  FlagReg flagreg_1 (
    .BusALU(alu_1_product), .RW(regcontroller_1_flag), .Clk_Clr({in_1, and_1_out[0]}), .ZF(ZF), .SF(SF),
    .CF(CF));  // open: CarryF
  Pull_Resistor pull_resistor_3 (.node(pull_resistor_3_node[0]));
  assign alu_1_product = pull_resistor_3_node[0] ? ram_1_dout : 8'bz;  // Controlled_Buffer controlled_buffer_1
  // Probe on alu_1_product
  Regs Accumulator (
    .DataIn(alu_1_product), .Clk_Clr({in_1, and_1_out[0]}), .RW(regcontroller_1_a),
    .CurrentData(Accumulator_currentdata), .DataOut(alu_1_product));
  Regs B (
    .DataIn(alu_1_product), .Clk_Clr({in_1, and_1_out[0]}), .RW(regcontroller_1_b),
    .CurrentData(B_currentdata), .DataOut(alu_1_product));
  Regs D (
    .DataIn(alu_1_product), .Clk_Clr({in_1, and_1_out[0]}), .RW(regcontroller_1_d),
    .CurrentData(D_currentdata), .DataOut(alu_1_product));
  Regs H (
    .DataIn(alu_1_product), .Clk_Clr({in_1, and_1_out[0]}), .RW(regcontroller_1_h),
    .CurrentData(H_currentdata), .DataOut(alu_1_product));
  jump jump_1 (.JMPData(MicroCode_data[19:17]), .ZF(ZF), .SF(SF), .JMP(jump_1_jmp));
  // Probe on Accumulator_currentdata
  // Probe on B_currentdata
  // Probe on D_currentdata
  // Probe on H_currentdata
  INCDEC incdec_1 (
    .RW(regcontroller_1_inc_dec), .CLK_CLR({in_1, and_1_out[0]}), .BusIn(alu_1_product), .ID(ID),
    .BusOut(alu_1_product));
  PC pc_1 (
    .LOAD(alu_1_product), .ByteSel(ByteSel), .Jump(jump_1_jmp), .RW(regcontroller_1_pc),
    .Clk_Clr({in_1, and_1_out[0]}), .BusData(alu_1_product));
  Stack stack_1 (
    .DataIn(alu_1_product), .RW(regcontroller_1_stack), .Clk_Clr({in_1, and_1_out[0]}), .ByteSel(ByteSel),
    .CurrentStack(stack_1_currentstack), .StackBus(alu_1_product));
  // Probe on stack_1_currentstack
  RegController regcontroller_1 (
    .RegAccess(RegAccess), .AccessType(RAType), .S0_S7RW(MicroCode_data[15:8]), .A(regcontroller_1_a),
    .temp(regcontroller_1_temp), .B(regcontroller_1_b), .C(regcontroller_1_c), .D(regcontroller_1_d),
    .E(regcontroller_1_e), .H(regcontroller_1_h), .L(regcontroller_1_l), .Flag(regcontroller_1_flag),
    .RAM(pull_resistor_3_node), .MAR(regcontroller_1_mar), .MDR(regcontroller_1_mdr),
    .IE(pull_resistor_2_node), .Stack(regcontroller_1_stack), .INC_DEC(regcontroller_1_inc_dec),
    .PC(regcontroller_1_pc));
  // Probe on Temp_currentdata
  Regs Temp (
    .DataIn(alu_1_product), .Clk_Clr({in_1, and_1_out[0]}), .RW(regcontroller_1_temp),
    .CurrentData(Temp_currentdata), .DataOut(alu_1_product));
  // Probe on C_currentdata
  Regs C (
    .DataIn(alu_1_product), .Clk_Clr({in_1, and_1_out[0]}), .RW(regcontroller_1_c),
    .CurrentData(C_currentdata), .DataOut(alu_1_product));
  // Probe on E_currentdata
  Regs E (
    .DataIn(alu_1_product), .Clk_Clr({in_1, and_1_out[0]}), .RW(regcontroller_1_e),
    .CurrentData(E_currentdata), .DataOut(alu_1_product));
  // Probe on L_currentdata
  Regs L (
    .DataIn(alu_1_product), .Clk_Clr({in_1, and_1_out[0]}), .RW(regcontroller_1_l),
    .CurrentData(L_currentdata), .DataOut(alu_1_product));

  // Other names for the same wires on the sheet: Clr = in_1; RUN = in_2

  // Notes on the sheet:
  //   contents of MicroCode (hex, n*v repeats v):
  //   af60 afe0 c960 8f40 92*0 af60 afe0 c960 8f40 af60 afe0 2960 8f40 200000 119*0 af60 afe0 c960 8f40
  //   af60 afe0 3960 8f40 200000 7*0 3 20c 4020 13*0 3 20c 3 244 3 224 90*0 af60 afe0 c960 8f40 af60 afe0
  //   4960 8f40 200000 119*0 af60 afe0 c960 8f40 af60 afe0 5960 8f40 200000 119*0 af60 afe0 c960 8f40 af60
  //   afe0 6960 8f40 200000 119*0 af60 afe0 c960 8f40 af60 afe0 7960 8f40 200000 55*0 3 20c 3 244 3 224
  //   4100 90 56*0 af60 afe0 c960 8f40 af60 afe0 8960 8f40 200000 55*0 af60 afe0 c960 8f40 af60 afe0 7960
  //   8f40 af60 afe0 6960 a760 a6e0 960 8f40 17*0 3 20c 248000 29*0 af60 afe0 c960 8f40 af60 afe0 960 8f40
  //   200000 890*0 100000 156*0 3 20c 21000 48000 12*0 3 20c 20800 48000 108*0 3 20c 21000 448000
endmodule

module uCodeDecoder (
  input  [3:0] in_1,
  input  [3:0] in_2,
  input  [23:0] in_3,
  input  [3:0] in_4,
  input  [3:0] in_5,
  input  [3:0] in_6,
  input  [3:0] in_7,
  output [3:0] out_8,
  output [3:0] out_9,
  output [3:0] out_10,
  output [3:0] out_11,
  output [23:0] out_12,
  output [3:0] out_13,
  output [3:0] out_14
);


  assign in_3[3:0] = {in_1[0], in_1[1], in_1[2], in_1[3]};
  assign out_8 = in_1;
  assign out_9 = {in_3[4], in_3[5], in_3[6], in_3[7]};
  assign out_10 = {in_3[8], in_3[9], in_3[10], in_3[11]};
  assign out_11 = {in_3[12], in_3[13], in_3[14], in_3[15]};
  assign out_12 = {in_7[0], in_7[1], in_7[2], in_7[3], in_6[0], in_6[1], in_6[2], in_6[3], in_5[0], in_5[1], in_5[2], in_5[3], in_4[0], in_4[1], in_4[2], in_4[3], in_2[0], in_2[1], in_2[2], in_2[3], in_1[0], in_1[1], in_1[2], in_1[3]};
  assign out_13 = {in_3[16], in_3[17], in_3[18], in_3[19]};
  assign out_14[3:1] = {in_3[20], in_3[21], in_3[22]};

  // Other names for the same wires on the sheet: ALUSel[3:0] = {in_1[0], in_1[1], in_1[2], in_1[3]}
endmodule

module PC (
  input  ByteSel,
  input  [7:0] LOAD,
  input  Jump,
  input  [1:0] RW,
  input  [1:0] Clk_Clr,
  output [7:0] BusData
);

  wire and_1_out, and_2_out, counter_1_carry;
  wire [7:0] controlled_buffer_1_out, counter_1_q, counter_2_q, demultiplexer_1_out0, demultiplexer_1_out1,
       multiplexer_1_out;

  assign controlled_buffer_1_out = Jump ? LOAD : 8'bz;  // Controlled_Buffer controlled_buffer_1
  Demultiplexer #(.width(8)) demultiplexer_1 (
    .out0(demultiplexer_1_out0), .out1(demultiplexer_1_out1), .in(controlled_buffer_1_out), .sel(ByteSel));
  and and_1 (and_1_out, Jump, ~RW[1], ~ByteSel);  // AND_Gate
  and and_2 (and_2_out, Jump, ByteSel);
  Counter counter_1 (
    .load(and_1_out), .D(demultiplexer_1_out0), .count(RW[1]), .Q(counter_1_q), .carry(counter_1_carry),
    .clk(Clk_Clr[0]), .clr(Clk_Clr[1]));  // open: up
  Multiplexer #(.width(8)) multiplexer_1 (.in0(counter_1_q), .in1(counter_2_q), .out(multiplexer_1_out), .sel(ByteSel));
  Counter counter_2 (
    .load(and_2_out), .D(demultiplexer_1_out1), .count(counter_1_carry), .Q(counter_2_q), .clk(Clk_Clr[0]),
    .clr(Clk_Clr[1]));  // open: carry, up
  assign BusData = RW[0] ? multiplexer_1_out : 8'bz;  // Controlled_Buffer controlled_buffer_2
endmodule

module Regs (
  input  [7:0] DataIn,
  input  [1:0] Clk_Clr,
  input  [1:0] RW,
  output [7:0] CurrentData,
  output [7:0] DataOut
);

  Register register_1 (.D(DataIn), .en(RW[1]), .Q(CurrentData), .clk(Clk_Clr[0]), .clr(Clk_Clr[1]));
  assign DataOut = RW[0] ? CurrentData : 8'bz;  // Controlled_Buffer controlled_buffer_1
endmodule

module FlagReg (
  input  [7:0] BusALU,
  input  CarryF,
  input  [1:0] RW,
  input  [1:0] Clk_Clr,
  output ZF,
  output SF,
  output CF
);

  wire [0:0] nor_1_out;
  wire [2:0] register_1_q;

  nor nor_1 (nor_1_out[0], BusALU[0], BusALU[1], BusALU[2], BusALU[3], BusALU[4], BusALU[5], BusALU[6], BusALU[7]);
  Register #(.width(3)) register_1 (
    .D({CarryF, BusALU[7], nor_1_out[0]}), .en(RW[0]), .Q(register_1_q), .clk(Clk_Clr[0]), .clr(Clk_Clr[1]));
  assign {CF, SF, ZF} = RW[1] ? register_1_q : 3'bz;  // Controlled_Buffer controlled_buffer_1
endmodule

module ALU (
  input  CFIn,
  input  [7:0] A,
  input  [3:0] ALUSel,
  input  [7:0] B,
  input  ALUOut,
  output CFOut,
  output [7:0] Product
);

  wire and_1_out, and_2_out, and_3_out, and_4_out, and_5_out, and_6_out, or_1_out, or_2_out;
  wire [7:0] addsubcomp_1_busline, and_7_out, multiplexer_1_out, or_3_out, undriven, xor_1_out;

  BarrelShifter barrelshifter_1 ();  // open: NumIn, ShiftAmt, NumOut
  and and_1 (and_1_out, ~ALUSel[0], ~ALUSel[1], ALUSel[2], ~ALUSel[3]);  // AND_Gate
  and and_2 (and_2_out, ALUSel[0], ~ALUSel[1], ~ALUSel[2], ~ALUSel[3]);  // AND_Gate
  and and_3 (and_3_out, ALUSel[0], ALUSel[1], ~ALUSel[2], ~ALUSel[3]);  // AND_Gate
  and and_4 (and_4_out, ~ALUSel[0], ALUSel[1], ~ALUSel[2], ~ALUSel[3]);  // AND_Gate
  or or_1 (or_1_out, and_2_out, and_3_out);
  or or_2 (or_2_out, and_4_out, and_3_out);
  and and_5 (and_5_out, and_1_out, CFIn);
  and and_6 (and_6_out, ~ALUSel[0], ALUSel[1], ALUSel[2], ~ALUSel[3]);  // AND_Gate
  AddSubComp addsubcomp_1 (
    .B(B), .Cin(and_5_out), .AddSub(or_1_out), .INC_DEC(or_2_out), .A(A), .BusLine(addsubcomp_1_busline));  // open: CF
  Complements complements_1 (.TwosComp(and_6_out), .A(A));  // open: BusLine, CF
  assign and_7_out = A & B;  // AND_Gate and_7, 8 bits wide
  assign or_3_out = A | B;  // OR_Gate or_3, 8 bits wide
  assign xor_1_out = A ^ B;  // XOR_Gate xor_1, 8 bits wide
  RLShifter rlshifter_1 ();  // open: NumIn, ShiftAmt, NumOut
  assign Product = ALUOut ? multiplexer_1_out : 8'bz;  // Controlled_Buffer controlled_buffer_1
  Multiplexer #(.select(4), .width(8)) multiplexer_1 (
    .in0(addsubcomp_1_busline), .in1(addsubcomp_1_busline), .in2(addsubcomp_1_busline),
    .in3(addsubcomp_1_busline), .in4(addsubcomp_1_busline), .in5(undriven), .in6(undriven), .in7(xor_1_out),
    .in8(and_7_out), .in9(or_3_out), .out(multiplexer_1_out), .sel(ALUSel));  // open: in10, in11, in12, in13, in14, in15

  // Notes on the sheet:
  //   00: Add
  //   01: Sub
  //   02: Inc
  //   03: Dec
  //   04: ADC
endmodule

module AddSubComp (
  input  Cin,
  input  [7:0] A,
  input  AddSub,
  input  INC_DEC,
  input  [7:0] B,
  output [7:0] BusLine,
  output CF
);

  wire or_1_out;
  wire [7:0] multiplexer_1_out, xor_1_out;

  Multiplexer #(.width(8)) multiplexer_1 (.in0(B), .in1(8'h1), .out(multiplexer_1_out), .sel(INC_DEC));
  or or_1 (or_1_out, Cin, AddSub);
  assign xor_1_out = {8{AddSub}} ^ multiplexer_1_out;  // XOR_Gate xor_1, 8 bits wide
  Adder adder_1 (.a(A), .b(xor_1_out), .out(BusLine), .cin(or_1_out), .cout(CF));
endmodule

module BarrelShifter (
  input  [7:0] NumIn,
  input  [3:0] ShiftAmt,
  output [7:0] NumOut
);

  wire multiplexer_1_out, multiplexer_2_out, multiplexer_3_out, multiplexer_4_out, multiplexer_5_out,
       multiplexer_6_out, multiplexer_7_out, multiplexer_8_out, multiplexer_9_out, multiplexer_10_out,
       multiplexer_11_out, multiplexer_12_out, multiplexer_13_out, multiplexer_14_out, multiplexer_15_out,
       multiplexer_16_out, multiplexer_17_out, multiplexer_18_out, multiplexer_19_out, multiplexer_20_out,
       multiplexer_21_out, multiplexer_22_out, multiplexer_23_out, multiplexer_24_out, multiplexer_25_out,
       multiplexer_26_out, multiplexer_27_out, multiplexer_28_out, multiplexer_29_out, multiplexer_30_out,
       multiplexer_31_out, multiplexer_32_out, not_1_out;

  Multiplexer multiplexer_1 (.in0(NumIn[0]), .in1(NumIn[7]), .out(multiplexer_1_out), .sel(not_1_out));
  Multiplexer multiplexer_2 (.in0(NumIn[1]), .in1(NumIn[6]), .out(multiplexer_2_out), .sel(not_1_out));
  Multiplexer multiplexer_3 (.in0(NumIn[2]), .in1(NumIn[5]), .out(multiplexer_3_out), .sel(not_1_out));
  Multiplexer multiplexer_4 (.in0(NumIn[3]), .in1(NumIn[4]), .out(multiplexer_4_out), .sel(not_1_out));
  Multiplexer multiplexer_5 (.in0(NumIn[4]), .in1(NumIn[3]), .out(multiplexer_5_out), .sel(not_1_out));
  Multiplexer multiplexer_6 (.in0(NumIn[5]), .in1(NumIn[2]), .out(multiplexer_6_out), .sel(not_1_out));
  Multiplexer multiplexer_7 (.in0(NumIn[6]), .in1(NumIn[1]), .out(multiplexer_7_out), .sel(not_1_out));
  Multiplexer multiplexer_8 (.in0(NumIn[7]), .in1(NumIn[0]), .out(multiplexer_8_out), .sel(not_1_out));
  Multiplexer multiplexer_9 (
    .in0(multiplexer_8_out), .in1(multiplexer_7_out), .out(multiplexer_9_out), .sel(ShiftAmt[0]));
  Multiplexer multiplexer_10 (
    .in0(multiplexer_7_out), .in1(multiplexer_6_out), .out(multiplexer_10_out), .sel(ShiftAmt[0]));
  Multiplexer multiplexer_11 (
    .in0(multiplexer_6_out), .in1(multiplexer_5_out), .out(multiplexer_11_out), .sel(ShiftAmt[0]));
  Multiplexer multiplexer_12 (
    .in0(multiplexer_5_out), .in1(multiplexer_4_out), .out(multiplexer_12_out), .sel(ShiftAmt[0]));
  Multiplexer multiplexer_13 (
    .in0(multiplexer_4_out), .in1(multiplexer_3_out), .out(multiplexer_13_out), .sel(ShiftAmt[0]));
  Multiplexer multiplexer_14 (
    .in0(multiplexer_3_out), .in1(multiplexer_2_out), .out(multiplexer_14_out), .sel(ShiftAmt[0]));
  Multiplexer multiplexer_15 (
    .in0(multiplexer_2_out), .in1(multiplexer_1_out), .out(multiplexer_15_out), .sel(ShiftAmt[0]));
  Multiplexer multiplexer_16 (
    .in0(multiplexer_1_out), .in1(multiplexer_8_out), .out(multiplexer_16_out), .sel(ShiftAmt[0]));
  not not_1 (not_1_out, ShiftAmt[3]);
  Multiplexer multiplexer_17 (
    .in0(multiplexer_9_out), .in1(multiplexer_11_out), .out(multiplexer_17_out), .sel(ShiftAmt[1]));
  Multiplexer multiplexer_18 (
    .in0(multiplexer_10_out), .in1(multiplexer_12_out), .out(multiplexer_18_out), .sel(ShiftAmt[1]));
  Multiplexer multiplexer_19 (
    .in0(multiplexer_11_out), .in1(multiplexer_13_out), .out(multiplexer_19_out), .sel(ShiftAmt[1]));
  Multiplexer multiplexer_20 (
    .in0(multiplexer_12_out), .in1(multiplexer_14_out), .out(multiplexer_20_out), .sel(ShiftAmt[1]));
  Multiplexer multiplexer_21 (
    .in0(multiplexer_13_out), .in1(multiplexer_15_out), .out(multiplexer_21_out), .sel(ShiftAmt[1]));
  Multiplexer multiplexer_22 (
    .in0(multiplexer_14_out), .in1(multiplexer_16_out), .out(multiplexer_22_out), .sel(ShiftAmt[1]));
  Multiplexer multiplexer_23 (
    .in0(multiplexer_15_out), .in1(multiplexer_9_out), .out(multiplexer_23_out), .sel(ShiftAmt[1]));
  Multiplexer multiplexer_24 (
    .in0(multiplexer_16_out), .in1(multiplexer_10_out), .out(multiplexer_24_out), .sel(ShiftAmt[1]));
  Multiplexer multiplexer_25 (
    .in0(multiplexer_17_out), .in1(multiplexer_21_out), .out(multiplexer_25_out), .sel(ShiftAmt[2]));
  Multiplexer multiplexer_26 (
    .in0(multiplexer_18_out), .in1(multiplexer_22_out), .out(multiplexer_26_out), .sel(ShiftAmt[2]));
  Multiplexer multiplexer_27 (
    .in0(multiplexer_19_out), .in1(multiplexer_23_out), .out(multiplexer_27_out), .sel(ShiftAmt[2]));
  Multiplexer multiplexer_28 (
    .in0(multiplexer_20_out), .in1(multiplexer_24_out), .out(multiplexer_28_out), .sel(ShiftAmt[2]));
  Multiplexer multiplexer_29 (
    .in0(multiplexer_21_out), .in1(multiplexer_17_out), .out(multiplexer_29_out), .sel(ShiftAmt[2]));
  Multiplexer multiplexer_30 (
    .in0(multiplexer_22_out), .in1(multiplexer_18_out), .out(multiplexer_30_out), .sel(ShiftAmt[2]));
  Multiplexer multiplexer_31 (
    .in0(multiplexer_23_out), .in1(multiplexer_19_out), .out(multiplexer_31_out), .sel(ShiftAmt[2]));
  Multiplexer multiplexer_32 (
    .in0(multiplexer_24_out), .in1(multiplexer_20_out), .out(multiplexer_32_out), .sel(ShiftAmt[2]));
  Multiplexer multiplexer_33 (.in0(multiplexer_32_out), .in1(multiplexer_25_out), .out(NumOut[0]), .sel(not_1_out));
  Multiplexer multiplexer_34 (.in0(multiplexer_31_out), .in1(multiplexer_26_out), .out(NumOut[1]), .sel(not_1_out));
  Multiplexer multiplexer_35 (.in0(multiplexer_30_out), .in1(multiplexer_27_out), .out(NumOut[2]), .sel(not_1_out));
  Multiplexer multiplexer_36 (.in0(multiplexer_29_out), .in1(multiplexer_28_out), .out(NumOut[3]), .sel(not_1_out));
  Multiplexer multiplexer_37 (.in0(multiplexer_28_out), .in1(multiplexer_29_out), .out(NumOut[4]), .sel(not_1_out));
  Multiplexer multiplexer_38 (.in0(multiplexer_27_out), .in1(multiplexer_30_out), .out(NumOut[5]), .sel(not_1_out));
  Multiplexer multiplexer_39 (.in0(multiplexer_26_out), .in1(multiplexer_31_out), .out(NumOut[6]), .sel(not_1_out));
  Multiplexer multiplexer_40 (.in0(multiplexer_25_out), .in1(multiplexer_32_out), .out(NumOut[7]), .sel(not_1_out));
endmodule

module RLShifter (
  input  [7:0] NumIn,
  input  [3:0] ShiftAmt,
  output [7:0] NumOut
);

  wire multiplexer_1_out, multiplexer_2_out, multiplexer_3_out, multiplexer_4_out, multiplexer_5_out,
       multiplexer_6_out, multiplexer_7_out, multiplexer_8_out, multiplexer_9_out, multiplexer_10_out,
       multiplexer_11_out, multiplexer_12_out, multiplexer_13_out, multiplexer_14_out, multiplexer_15_out,
       multiplexer_16_out, multiplexer_17_out, multiplexer_18_out, multiplexer_19_out, multiplexer_20_out,
       multiplexer_21_out, multiplexer_22_out, multiplexer_23_out, multiplexer_24_out, multiplexer_25_out,
       multiplexer_26_out, multiplexer_27_out, multiplexer_28_out, multiplexer_29_out, multiplexer_30_out,
       multiplexer_31_out, multiplexer_32_out;

  Multiplexer multiplexer_1 (.in0(NumIn[0]), .in1(NumIn[7]), .out(multiplexer_1_out), .sel(ShiftAmt[3]));
  Multiplexer multiplexer_2 (.in0(NumIn[1]), .in1(NumIn[6]), .out(multiplexer_2_out), .sel(ShiftAmt[3]));
  Multiplexer multiplexer_3 (.in0(NumIn[2]), .in1(NumIn[5]), .out(multiplexer_3_out), .sel(ShiftAmt[3]));
  Multiplexer multiplexer_4 (.in0(NumIn[3]), .in1(NumIn[4]), .out(multiplexer_4_out), .sel(ShiftAmt[3]));
  Multiplexer multiplexer_5 (.in0(NumIn[4]), .in1(NumIn[3]), .out(multiplexer_5_out), .sel(ShiftAmt[3]));
  Multiplexer multiplexer_6 (.in0(NumIn[5]), .in1(NumIn[2]), .out(multiplexer_6_out), .sel(ShiftAmt[3]));
  Multiplexer multiplexer_7 (.in0(NumIn[6]), .in1(NumIn[1]), .out(multiplexer_7_out), .sel(ShiftAmt[3]));
  Multiplexer multiplexer_8 (.in0(NumIn[7]), .in1(NumIn[0]), .out(multiplexer_8_out), .sel(ShiftAmt[3]));
  Multiplexer multiplexer_9 (
    .in0(multiplexer_1_out), .in1(multiplexer_2_out), .out(multiplexer_9_out), .sel(ShiftAmt[0]));
  Multiplexer multiplexer_10 (
    .in0(multiplexer_2_out), .in1(multiplexer_3_out), .out(multiplexer_10_out), .sel(ShiftAmt[0]));
  Multiplexer multiplexer_11 (
    .in0(multiplexer_3_out), .in1(multiplexer_4_out), .out(multiplexer_11_out), .sel(ShiftAmt[0]));
  Multiplexer multiplexer_12 (
    .in0(multiplexer_4_out), .in1(multiplexer_5_out), .out(multiplexer_12_out), .sel(ShiftAmt[0]));
  Multiplexer multiplexer_13 (
    .in0(multiplexer_5_out), .in1(multiplexer_6_out), .out(multiplexer_13_out), .sel(ShiftAmt[0]));
  Multiplexer multiplexer_14 (
    .in0(multiplexer_6_out), .in1(multiplexer_7_out), .out(multiplexer_14_out), .sel(ShiftAmt[0]));
  Multiplexer multiplexer_15 (
    .in0(multiplexer_7_out), .in1(multiplexer_8_out), .out(multiplexer_15_out), .sel(ShiftAmt[0]));
  Multiplexer multiplexer_16 (.in0(multiplexer_8_out), .in1(1'b0), .out(multiplexer_16_out), .sel(ShiftAmt[0]));
  Multiplexer multiplexer_17 (
    .in0(multiplexer_9_out), .in1(multiplexer_11_out), .out(multiplexer_17_out), .sel(ShiftAmt[1]));
  Multiplexer multiplexer_18 (
    .in0(multiplexer_10_out), .in1(multiplexer_12_out), .out(multiplexer_18_out), .sel(ShiftAmt[1]));
  Multiplexer multiplexer_19 (
    .in0(multiplexer_11_out), .in1(multiplexer_13_out), .out(multiplexer_19_out), .sel(ShiftAmt[1]));
  Multiplexer multiplexer_20 (
    .in0(multiplexer_12_out), .in1(multiplexer_14_out), .out(multiplexer_20_out), .sel(ShiftAmt[1]));
  Multiplexer multiplexer_21 (
    .in0(multiplexer_13_out), .in1(multiplexer_15_out), .out(multiplexer_21_out), .sel(ShiftAmt[1]));
  Multiplexer multiplexer_22 (
    .in0(multiplexer_14_out), .in1(multiplexer_16_out), .out(multiplexer_22_out), .sel(ShiftAmt[1]));
  Multiplexer multiplexer_23 (.in0(multiplexer_15_out), .in1(1'b0), .out(multiplexer_23_out), .sel(ShiftAmt[1]));
  Multiplexer multiplexer_24 (.in0(multiplexer_16_out), .in1(1'b0), .out(multiplexer_24_out), .sel(ShiftAmt[1]));
  Multiplexer multiplexer_25 (
    .in0(multiplexer_17_out), .in1(multiplexer_21_out), .out(multiplexer_25_out), .sel(ShiftAmt[2]));
  Multiplexer multiplexer_26 (
    .in0(multiplexer_18_out), .in1(multiplexer_22_out), .out(multiplexer_26_out), .sel(ShiftAmt[2]));
  Multiplexer multiplexer_27 (
    .in0(multiplexer_19_out), .in1(multiplexer_23_out), .out(multiplexer_27_out), .sel(ShiftAmt[2]));
  Multiplexer multiplexer_28 (
    .in0(multiplexer_20_out), .in1(multiplexer_24_out), .out(multiplexer_28_out), .sel(ShiftAmt[2]));
  Multiplexer multiplexer_29 (.in0(multiplexer_21_out), .in1(1'b0), .out(multiplexer_29_out), .sel(ShiftAmt[2]));
  Multiplexer multiplexer_30 (.in0(multiplexer_22_out), .in1(1'b0), .out(multiplexer_30_out), .sel(ShiftAmt[2]));
  Multiplexer multiplexer_31 (.in0(multiplexer_23_out), .in1(1'b0), .out(multiplexer_31_out), .sel(ShiftAmt[2]));
  Multiplexer multiplexer_32 (.in0(multiplexer_24_out), .in1(1'b0), .out(multiplexer_32_out), .sel(ShiftAmt[2]));
  Multiplexer multiplexer_33 (.in0(multiplexer_25_out), .in1(multiplexer_32_out), .out(NumOut[0]), .sel(ShiftAmt[3]));
  Multiplexer multiplexer_34 (.in0(multiplexer_26_out), .in1(multiplexer_31_out), .out(NumOut[1]), .sel(ShiftAmt[3]));
  Multiplexer multiplexer_35 (.in0(multiplexer_27_out), .in1(multiplexer_30_out), .out(NumOut[2]), .sel(ShiftAmt[3]));
  Multiplexer multiplexer_36 (.in0(multiplexer_28_out), .in1(multiplexer_29_out), .out(NumOut[3]), .sel(ShiftAmt[3]));
  Multiplexer multiplexer_37 (.in0(multiplexer_29_out), .in1(multiplexer_28_out), .out(NumOut[4]), .sel(ShiftAmt[3]));
  Multiplexer multiplexer_38 (.in0(multiplexer_30_out), .in1(multiplexer_27_out), .out(NumOut[5]), .sel(ShiftAmt[3]));
  Multiplexer multiplexer_39 (.in0(multiplexer_31_out), .in1(multiplexer_26_out), .out(NumOut[6]), .sel(ShiftAmt[3]));
  Multiplexer multiplexer_40 (.in0(multiplexer_32_out), .in1(multiplexer_25_out), .out(NumOut[7]), .sel(ShiftAmt[3]));

  // Notes on the sheet:
  //   Bit 4 R L Select
endmodule

module Complements (
  input  TwosComp,
  input  [7:0] A,
  output [7:0] BusLine,
  output CF
);

  wire [7:0] xor_1_out;

  Adder adder_1 (.a({8{1'b0}}), .b(xor_1_out), .out(BusLine), .cin(TwosComp), .cout(CF));
  assign xor_1_out = {8{TwosComp}} ^ A;  // XOR_Gate xor_1, 8 bits wide
endmodule

module Display (
  input  UpperLoad,
  input  [7:0] BusLine,
  input  LowerLoad,
  input  [1:0] Clk_Clr,
  input  DisEn,
  output [7:0] Ones,
  output [7:0] Tens,
  output [7:0] Hundreds,
  output [7:0] Thousands,
  output [7:0] TenThousands
);

  wire [7:0] register_1_q, register_2_q;
  wire [39:0] UnsignedROM_data;

  Register register_1 (.D(BusLine), .en(UpperLoad), .Q(register_1_q), .clk(Clk_Clr[0]), .clr(Clk_Clr[1]));
  Register register_2 (.D(BusLine), .en(LowerLoad), .Q(register_2_q), .clk(Clk_Clr[0]), .clr(Clk_Clr[1]));
  ROM #(.addrWidth(16), .dataWidth(40)) UnsignedROM (.addr({register_1_q, register_2_q}), .data(UnsignedROM_data));
  Register #(.width(40)) register_3 (
    .D(UnsignedROM_data), .en(DisEn), .Q({TenThousands, Thousands, Hundreds, Tens, Ones}), .clk(Clk_Clr[0]),
    .clr(Clk_Clr[1]));

  // Notes on the sheet:
  //   contents of UnsignedROM (hex, n*v repeats v):
  //   3f3f3f3f3f 3f3f3f3f06 3f3f3f3f5b 3f3f3f3f4f 3f3f3f3f66 3f3f3f3f6d 3f3f3f3f7c 3f3f3f3f07 3f3f3f3f7f
  //   3f3f3f3f67 3f3f3f063f 3f3f3f0606 3f3f3f065b 3f3f3f064f 3f3f3f0666 3f3f3f066d 3f3f3f067c 3f3f3f0607
  //   3f3f3f067f 3f3f3f0667 3f3f3f5b3f 3f3f3f5b06 3f3f3f5b5b 3f3f3f5b4f 3f3f3f5b66 3f3f3f5b6d 3f3f3f5b7c
  //   3f3f3f5b07 3f3f3f5b7f 3f3f3f5b67 3f3f3f4f3f 3f3f3f4f06 3f3f3f4f5b 3f3f3f4f4f 3f3f3f4f66 3f3f3f4f6d
  //   3f3f3f4f7c 3f3f3f4f07 3f3f3f4f7f 3f3f3f4f67 3f3f3f663f 3f3f3f6606 3f3f3f665b 3f3f3f664f 3f3f3f6666
  //   3f3f3f666d 3f3f3f667c 3f3f3f6607 3f3f3f667f 3f3f3f6667 3f3f3f6d3f 3f3f3f6d06 3f3f3f6d5b 3f3f3f6d4f
  //   3f3f3f6d66 3f3f3f6d6d 3f3f3f6d7c 3f3f3f6d07 3f3f3f6d7f 3f3f3f6d67 3f3f3f7c3f 3f3f3f7c06 3f3f3f7c5b
  //   3f3f3f7c4f 3f3f3f7c66 3f3f3f7c6d 3f3f3f7c7c 3f3f3f7c07 3f3f3f7c7f 3f3f3f7c67 3f3f3f073f 3f3f3f0706
  //   3f3f3f075b 3f3f3f074f 3f3f3f0766 3f3f3f076d 3f3f3f077c 3f3f3f0707 3f3f3f077f 3f3f3f0767 3f3f3f7f3f
  //   3f3f3f7f06 3f3f3f7f5b 3f3f3f7f4f 3f3f3f7f66 3f3f3f7f6d 3f3f3f7f7c 3f3f3f7f07 3f3f3f7f7f 3f3f3f7f67
  //   3f3f3f673f 3f3f3f6706 3f3f3f675b 3f3f3f674f 3f3f3f6766 3f3f3f676d 3f3f3f677c 3f3f3f6707 3f3f3f677f
  //   3f3f3f6767 3f3f063f3f 3f3f063f06 3f3f063f5b 3f3f063f4f 3f3f063f66 3f3f063f6d 3f3f063f7c 3f3f063f07
  //   3f3f063f7f 3f3f063f67 3f3f06063f 3f3f060606 3f3f06065b 3f3f06064f 3f3f060666 3f3f06066d 3f3f06067c
  //   3f3f060607 3f3f06067f 3f3f060667 3f3f065b3f 3f3f065b06 3f3f065b5b 3f3f065b4f 3f3f065b66 3f3f065b6d
  //   3f3f065b7c 3f3f065b07 3f3f065b7f 3f3f065b67 3f3f064f3f 3f3f064f06 3f3f064f5b 3f3f064f4f 3f3f064f66
  //   3f3f064f6d 3f3f064f7c 3f3f064f07 3f3f064f7f 3f3f064f67 3f3f06663f 3f3f066606 3f3f06665b 3f3f06664f
  //   3f3f066666 3f3f06666d 3f3f06667c 3f3f066607 3f3f06667f 3f3f066667 3f3f066d3f 3f3f066d06 3f3f066d5b
  //   3f3f066d4f 3f3f066d66 3f3f066d6d 3f3f066d7c 3f3f066d07 3f3f066d7f 3f3f066d67 3f3f067c3f 3f3f067c06
  //   3f3f067c5b 3f3f067c4f 3f3f067c66 3f3f067c6d 3f3f067c7c 3f3f067c07 3f3f067c7f 3f3f067c67 3f3f06073f
  //   3f3f060706 3f3f06075b 3f3f06074f 3f3f060766 3f3f06076d 3f3f06077c 3f3f060707 3f3f06077f 3f3f060767
  //   3f3f067f3f 3f3f067f06 3f3f067f5b 3f3f067f4f 3f3f067f66 3f3f067f6d 3f3f067f7c 3f3f067f07 3f3f067f7f
  //   3f3f067f67 3f3f06673f 3f3f066706 3f3f06675b 3f3f06674f 3f3f066766 3f3f06676d 3f3f06677c 3f3f066707
  //   3f3f06677f 3f3f066767 3f3f5b3f3f 3f3f5b3f06 3f3f5b3f5b 3f3f5b3f4f 3f3f5b3f66 3f3f5b3f6d 3f3f5b3f7c
  //   3f3f5b3f07 3f3f5b3f7f 3f3f5b3f67 3f3f5b063f 3f3f5b0606 3f3f5b065b 3f3f5b064f 3f3f5b0666 3f3f5b066d
  //   3f3f5b067c 3f3f5b0607 3f3f5b067f 3f3f5b0667 3f3f5b5b3f 3f3f5b5b06 3f3f5b5b5b 3f3f5b5b4f 3f3f5b5b66
  //   3f3f5b5b6d 3f3f5b5b7c 3f3f5b5b07 3f3f5b5b7f 3f3f5b5b67 3f3f5b4f3f 3f3f5b4f06 3f3f5b4f5b 3f3f5b4f4f
  //   3f3f5b4f66 3f3f5b4f6d 3f3f5b4f7c 3f3f5b4f07 3f3f5b4f7f 3f3f5b4f67 3f3f5b663f 3f3f5b6606 3f3f5b665b
  //   3f3f5b664f 3f3f5b6666 3f3f5b666d 3f3f5b667c 3f3f5b6607 3f3f5b667f 3f3f5b6667 3f3f5b6d3f 3f3f5b6d06
  //   3f3f5b6d5b 3f3f5b6d4f 3f3f5b6d66 3f3f5b6d6d 3f3f5b6d7c 3f3f5b6d07 3f3f5b6d7f 3f3f5b6d67 3f3f5b7c3f
  //   3f3f5b7c06 3f3f5b7c5b 3f3f5b7c4f 3f3f5b7c66 3f3f5b7c6d 3f3f5b7c7c 3f3f5b7c07 3f3f5b7c7f 3f3f5b7c67
  //   3f3f5b073f 3f3f5b0706 3f3f5b075b 3f3f5b074f 3f3f5b0766 3f3f5b076d 3f3f5b077c 3f3f5b0707 3f3f5b077f
  //   3f3f5b0767 3f3f5b7f3f 3f3f5b7f06 3f3f5b7f5b 3f3f5b7f4f 3f3f5b7f66 3f3f5b7f6d 3f3f5b7f7c 3f3f5b7f07
  //   3f3f5b7f7f 3f3f5b7f67 3f3f5b673f 3f3f5b6706 3f3f5b675b 3f3f5b674f 3f3f5b6766 3f3f5b676d 3f3f5b677c
  //   3f3f5b6707 3f3f5b677f 3f3f5b6767 3f3f4f3f3f 3f3f4f3f06 3f3f4f3f5b 3f3f4f3f4f 3f3f4f3f66 3f3f4f3f6d
  //   3f3f4f3f7c 3f3f4f3f07 3f3f4f3f7f 3f3f4f3f67 3f3f4f063f 3f3f4f0606 3f3f4f065b 3f3f4f064f 3f3f4f0666
  //   3f3f4f066d 3f3f4f067c 3f3f4f0607 3f3f4f067f 3f3f4f0667 3f3f4f5b3f 3f3f4f5b06 3f3f4f5b5b 3f3f4f5b4f
  //   3f3f4f5b66 3f3f4f5b6d 3f3f4f5b7c 3f3f4f5b07 3f3f4f5b7f 3f3f4f5b67 3f3f4f4f3f 3f3f4f4f06 3f3f4f4f5b
  //   3f3f4f4f4f 3f3f4f4f66 3f3f4f4f6d 3f3f4f4f7c 3f3f4f4f07 3f3f4f4f7f 3f3f4f4f67 3f3f4f663f 3f3f4f6606
  //   3f3f4f665b 3f3f4f664f 3f3f4f6666 3f3f4f666d 3f3f4f667c 3f3f4f6607 3f3f4f667f 3f3f4f6667 3f3f4f6d3f
  //   3f3f4f6d06 3f3f4f6d5b 3f3f4f6d4f 3f3f4f6d66 3f3f4f6d6d 3f3f4f6d7c 3f3f4f6d07 3f3f4f6d7f 3f3f4f6d67
  //   3f3f4f7c3f 3f3f4f7c06 3f3f4f7c5b 3f3f4f7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
endmodule

module ROMTEst (
  input  [15:0] in_1,
  input  UpperLoad,
  input  [7:0] BusLine,
  input  LowerLoad,
  input  Clk,
  input  Reset,
  input  DisEn,
  output [7:0] Ones,
  output [7:0] Tens,
  output [7:0] Hundreds,
  output [7:0] Thousands,
  output [7:0] TenThousands
);

  wire [7:0] register_1_q, register_2_q;
  wire [39:0] rom_1_data;

  Register register_1 (.D(BusLine), .en(UpperLoad), .Q(register_1_q), .clk(Clk), .clr(Reset));
  Register register_2 (.D(BusLine), .en(LowerLoad), .Q(register_2_q), .clk(Clk), .clr(Reset));
  _7_Segment_Display u_7_segment_display_1 (
    .g(TenThousands[6]), .f(TenThousands[5]), .a(TenThousands[0]), .b(TenThousands[1]), .e(TenThousands[4]),
    .d(TenThousands[3]), .c(TenThousands[2]));  // open: dp
  ROM #(.addrWidth(16), .dataWidth(40)) rom_1 (.addr(in_1), .data(rom_1_data));
  _7_Segment_Display u_7_segment_display_2 (
    .g(Thousands[6]), .f(Thousands[5]), .a(Thousands[0]), .b(Thousands[1]), .e(Thousands[4]),
    .d(Thousands[3]), .c(Thousands[2]));  // open: dp
  _7_Segment_Display u_7_segment_display_3 (
    .g(Hundreds[6]), .f(Hundreds[5]), .a(Hundreds[0]), .b(Hundreds[1]), .e(Hundreds[4]), .d(Hundreds[3]),
    .c(Hundreds[2]));  // open: dp
  _7_Segment_Display u_7_segment_display_4 (
    .g(Tens[6]), .f(Tens[5]), .a(Tens[0]), .b(Tens[1]), .e(Tens[4]), .d(Tens[3]), .c(Tens[2]));  // open: dp
  Register #(.width(40)) register_3 (
    .D(rom_1_data), .en(DisEn), .Q({TenThousands, Thousands, Hundreds, Tens, Ones}), .clk(Clk), .clr(Reset));
  _7_Segment_Display u_7_segment_display_5 (
    .g(Ones[6]), .f(Ones[5]), .a(Ones[0]), .b(Ones[1]), .e(Ones[4]), .d(Ones[3]), .c(Ones[2]));  // open: dp

  // Notes on the sheet:
  //   contents of rom_1 (hex, n*v repeats v):
  //   3f3f3f3f3f 3f3f3f3f06 3f3f3f3f5b 3f3f3f3f4f 3f3f3f3f66 3f3f3f3f6d 3f3f3f3f7c 3f3f3f3f07 3f3f3f3f7f
  //   3f3f3f3f67 3f3f3f063f 3f3f3f0606 3f3f3f065b 3f3f3f064f 3f3f3f0666 3f3f3f066d 3f3f3f067c 3f3f3f0607
  //   3f3f3f067f 3f3f3f0667 3f3f3f5b3f 3f3f3f5b06 3f3f3f5b5b 3f3f3f5b4f 3f3f3f5b66 3f3f3f5b6d 3f3f3f5b7c
  //   3f3f3f5b07 3f3f3f5b7f 3f3f3f5b67 3f3f3f4f3f 3f3f3f4f06 3f3f3f4f5b 3f3f3f4f4f 3f3f3f4f66 3f3f3f4f6d
  //   3f3f3f4f7c 3f3f3f4f07 3f3f3f4f7f 3f3f3f4f67 3f3f3f663f 3f3f3f6606 3f3f3f665b 3f3f3f664f 3f3f3f6666
  //   3f3f3f666d 3f3f3f667c 3f3f3f6607 3f3f3f667f 3f3f3f6667 3f3f3f6d3f 3f3f3f6d06 3f3f3f6d5b 3f3f3f6d4f
  //   3f3f3f6d66 3f3f3f6d6d 3f3f3f6d7c 3f3f3f6d07 3f3f3f6d7f 3f3f3f6d67 3f3f3f7c3f 3f3f3f7c06 3f3f3f7c5b
  //   3f3f3f7c4f 3f3f3f7c66 3f3f3f7c6d 3f3f3f7c7c 3f3f3f7c07 3f3f3f7c7f 3f3f3f7c67 3f3f3f073f 3f3f3f0706
  //   3f3f3f075b 3f3f3f074f 3f3f3f0766 3f3f3f076d 3f3f3f077c 3f3f3f0707 3f3f3f077f 3f3f3f0767 3f3f3f7f3f
  //   3f3f3f7f06 3f3f3f7f5b 3f3f3f7f4f 3f3f3f7f66 3f3f3f7f6d 3f3f3f7f7c 3f3f3f7f07 3f3f3f7f7f 3f3f3f7f67
  //   3f3f3f673f 3f3f3f6706 3f3f3f675b 3f3f3f674f 3f3f3f6766 3f3f3f676d 3f3f3f677c 3f3f3f6707 3f3f3f677f
  //   3f3f3f6767 3f3f063f3f 3f3f063f06 3f3f063f5b 3f3f063f4f 3f3f063f66 3f3f063f6d 3f3f063f7c 3f3f063f07
  //   3f3f063f7f 3f3f063f67 3f3f06063f 3f3f060606 3f3f06065b 3f3f06064f 3f3f060666 3f3f06066d 3f3f06067c
  //   3f3f060607 3f3f06067f 3f3f060667 3f3f065b3f 3f3f065b06 3f3f065b5b 3f3f065b4f 3f3f065b66 3f3f065b6d
  //   3f3f065b7c 3f3f065b07 3f3f065b7f 3f3f065b67 3f3f064f3f 3f3f064f06 3f3f064f5b 3f3f064f4f 3f3f064f66
  //   3f3f064f6d 3f3f064f7c 3f3f064f07 3f3f064f7f 3f3f064f67 3f3f06663f 3f3f066606 3f3f06665b 3f3f06664f
  //   3f3f066666 3f3f06666d 3f3f06667c 3f3f066607 3f3f06667f 3f3f066667 3f3f066d3f 3f3f066d06 3f3f066d5b
  //   3f3f066d4f 3f3f066d66 3f3f066d6d 3f3f066d7c 3f3f066d07 3f3f066d7f 3f3f066d67 3f3f067c3f 3f3f067c06
  //   3f3f067c5b 3f3f067c4f 3f3f067c66 3f3f067c6d 3f3f067c7c 3f3f067c07 3f3f067c7f 3f3f067c67 3f3f06073f
  //   3f3f060706 3f3f06075b 3f3f06074f 3f3f060766 3f3f06076d 3f3f06077c 3f3f060707 3f3f06077f 3f3f060767
  //   3f3f067f3f 3f3f067f06 3f3f067f5b 3f3f067f4f 3f3f067f66 3f3f067f6d 3f3f067f7c 3f3f067f07 3f3f067f7f
  //   3f3f067f67 3f3f06673f 3f3f066706 3f3f06675b 3f3f06674f 3f3f066766 3f3f06676d 3f3f06677c 3f3f066707
  //   3f3f06677f 3f3f066767 3f3f5b3f3f 3f3f5b3f06 3f3f5b3f5b 3f3f5b3f4f 3f3f5b3f66 3f3f5b3f6d 3f3f5b3f7c
  //   3f3f5b3f07 3f3f5b3f7f 3f3f5b3f67 3f3f5b063f 3f3f5b0606 3f3f5b065b 3f3f5b064f 3f3f5b0666 3f3f5b066d
  //   3f3f5b067c 3f3f5b0607 3f3f5b067f 3f3f5b0667 3f3f5b5b3f 3f3f5b5b06 3f3f5b5b5b 3f3f5b5b4f 3f3f5b5b66
  //   3f3f5b5b6d 3f3f5b5b7c 3f3f5b5b07 3f3f5b5b7f 3f3f5b5b67 3f3f5b4f3f 3f3f5b4f06 3f3f5b4f5b 3f3f5b4f4f
  //   3f3f5b4f66 3f3f5b4f6d 3f3f5b4f7c 3f3f5b4f07 3f3f5b4f7f 3f3f5b4f67 3f3f5b663f 3f3f5b6606 3f3f5b665b
  //   3f3f5b664f 3f3f5b6666 3f3f5b666d 3f3f5b667c 3f3f5b6607 3f3f5b667f 3f3f5b6667 3f3f5b6d3f 3f3f5b6d06
  //   3f3f5b6d5b 3f3f5b6d4f 3f3f5b6d66 3f3f5b6d6d 3f3f5b6d7c 3f3f5b6d07 3f3f5b6d7f 3f3f5b6d67 3f3f5b7c3f
  //   3f3f5b7c06 3f3f5b7c5b 3f3f5b7c4f 3f3f5b7c66 3f3f5b7c6d 3f3f5b7c7c 3f3f5b7c07 3f3f5b7c7f 3f3f5b7c67
  //   3f3f5b073f 3f3f5b0706 3f3f5b075b 3f3f5b074f 3f3f5b0766 3f3f5b076d 3f3f5b077c 3f3f5b0707 3f3f5b077f
  //   3f3f5b0767 3f3f5b7f3f 3f3f5b7f06 3f3f5b7f5b 3f3f5b7f4f 3f3f5b7f66 3f3f5b7f6d 3f3f5b7f7c 3f3f5b7f07
  //   3f3f5b7f7f 3f3f5b7f67 3f3f5b673f 3f3f5b6706 3f3f5b675b 3f3f5b674f 3f3f5b6766 3f3f5b676d 3f3f5b677c
  //   3f3f5b6707 3f3f5b677f 3f3f5b6767 3f3f4f3f3f 3f3f4f3f06 3f3f4f3f5b 3f3f4f3f4f 3f3f4f3f66 3f3f4f3f6d
  //   3f3f4f3f7c 3f3f4f3f07 3f3f4f3f7f 3f3f4f3f67 3f3f4f063f 3f3f4f0606 3f3f4f065b 3f3f4f064f 3f3f4f0666
  //   3f3f4f066d 3f3f4f067c 3f3f4f0607 3f3f4f067f 3f3f4f0667 3f3f4f5b3f 3f3f4f5b06 3f3f4f5b5b 3f3f4f5b4f
  //   3f3f4f5b66 3f3f4f5b6d 3f3f4f5b7c 3f3f4f5b07 3f3f4f5b7f 3f3f4f5b67 3f3f4f4f3f 3f3f4f4f06 3f3f4f4f5b
  //   3f3f4f4f4f 3f3f4f4f66 3f3f4f4f6d 3f3f4f4f7c 3f3f4f4f07 3f3f4f4f7f 3f3f4f4f67 3f3f4f663f 3f3f4f6606
  //   3f3f4f665b 3f3f4f664f 3f3f4f6666 3f3f4f666d 3f3f4f667c 3f3f4f6607 3f3f4f667f 3f3f4f6667 3f3f4f6d3f
  //   3f3f4f6d06 3f3f4f6d5b 3f3f4f6d4f 3f3f4f6d66 3f3f4f6d6d 3f3f4f6d7c 3f3f4f6d07 3f3f4f6d7f 3f3f4f6d67
  //   3f3f4f7c3f 3f3f4f7c06 3f3f4f7c5b 3f3f4f7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
endmodule

module RAMController (
  input  ByteSel,
  input  [7:0] MAR,
  input  MAREn,
  input  MDREn,
  input  [1:0] Clk_Clr,
  output [15:0] Addr,
  output [7:0] RAMWr
);

  wire and_1_out, xor_1_out;
  wire [7:0] controlled_buffer_1_out, demultiplexer_1_out0, demultiplexer_1_out1;

  assign controlled_buffer_1_out = MAREn ? MAR : 8'bz;  // Controlled_Buffer controlled_buffer_1
  and and_1 (and_1_out, ByteSel, MAREn);
  Demultiplexer #(.width(8)) demultiplexer_1 (
    .out0(demultiplexer_1_out0), .out1(demultiplexer_1_out1), .in(controlled_buffer_1_out), .sel(ByteSel));
  xor xor_1 (xor_1_out, ByteSel, MAREn);
  Register register_1 (.D(demultiplexer_1_out1), .en(and_1_out), .Q(Addr[15:8]), .clk(Clk_Clr[0]), .clr(Clk_Clr[1]));
  Register register_2 (.D(demultiplexer_1_out0), .en(xor_1_out), .Q(Addr[7:0]), .clk(Clk_Clr[0]), .clr(Clk_Clr[1]));
  Register register_3 (.D(MAR), .en(MDREn), .Q(RAMWr), .clk(Clk_Clr[0]), .clr(Clk_Clr[1]));
endmodule

module Stack (
  input  ByteSel,
  input  [7:0] DataIn,
  input  [1:0] RW,
  input  [1:0] Clk_Clr,
  output [7:0] StackBus,
  output [15:0] CurrentStack
);

  wire and_1_out, and_2_out;
  wire [7:0] controlled_buffer_1_out, demultiplexer_1_out0, demultiplexer_1_out1, multiplexer_1_out;

  assign controlled_buffer_1_out = RW[1] ? DataIn : 8'bz;  // Controlled_Buffer controlled_buffer_1
  and and_1 (and_1_out, RW[1], ByteSel);
  and and_2 (and_2_out, RW[1], ~ByteSel);  // AND_Gate
  Demultiplexer #(.width(8)) demultiplexer_1 (
    .out0(demultiplexer_1_out0), .out1(demultiplexer_1_out1), .in(controlled_buffer_1_out), .sel(ByteSel));
  Register register_1 (
    .D(demultiplexer_1_out1), .en(and_1_out), .Q(CurrentStack[15:8]), .clk(Clk_Clr[0]), .clr(Clk_Clr[1]));
  Register register_2 (
    .D(demultiplexer_1_out0), .en(and_2_out), .Q(CurrentStack[7:0]), .clk(Clk_Clr[0]), .clr(Clk_Clr[1]));
  Multiplexer #(.width(8)) multiplexer_1 (
    .in0(CurrentStack[7:0]), .in1(CurrentStack[15:8]), .out(multiplexer_1_out), .sel(RW[1]));
  assign StackBus = RW[0] ? multiplexer_1_out : 8'bz;  // Controlled_Buffer controlled_buffer_2
endmodule

module RegController (
  input  RegAccess,
  input  AccessType,
  input  [7:0] S0_S7RW,
  output [1:0] A,
  output [1:0] temp,
  output [1:0] B,
  output [1:0] C,
  output [1:0] D,
  output [1:0] E,
  output [1:0] H,
  output [1:0] L,
  output [1:0] Flag,
  output [1:0] RAM,
  output [1:0] MAR,
  output [1:0] MDR,
  output [1:0] IE,
  output [1:0] Stack,
  output [1:0] INC_DEC,
  output [1:0] PC
);

  wire not_1_out;
  wire [1:0] demultiplexer_1_out0, demultiplexer_1_out1, demultiplexer_1_out2, demultiplexer_1_out3,
       demultiplexer_1_out4, demultiplexer_1_out5, demultiplexer_1_out6, demultiplexer_1_out7,
       demultiplexer_1_out8, demultiplexer_1_out9, demultiplexer_1_out10, demultiplexer_1_out11,
       demultiplexer_1_out12, demultiplexer_1_out13, demultiplexer_1_out14, demultiplexer_1_out15,
       demultiplexer_2_out0, demultiplexer_2_out1, demultiplexer_2_out2, demultiplexer_2_out3,
       demultiplexer_2_out4, demultiplexer_2_out5, demultiplexer_2_out6, demultiplexer_2_out7,
       demultiplexer_2_out8, demultiplexer_2_out9, demultiplexer_2_out10, demultiplexer_2_out11,
       demultiplexer_2_out12, demultiplexer_2_out13, demultiplexer_2_out14, demultiplexer_2_out15,
       demultiplexer_3_out0, demultiplexer_3_out1, demultiplexer_3_out2, demultiplexer_3_out3,
       demultiplexer_3_out4, demultiplexer_3_out5, demultiplexer_3_out6, demultiplexer_3_out7,
       demultiplexer_3_out8, demultiplexer_3_out9, demultiplexer_3_out10, demultiplexer_3_out11,
       demultiplexer_3_out12, demultiplexer_3_out13, demultiplexer_3_out14, demultiplexer_3_out15, nand_1_out;
  wire [7:0] controlled_buffer_1_out, controlled_buffer_2_out;
  wire [31:0] controlled_buffer_3_out, multiplexer_1_out, or_1_out;
  wire [63:0] controlled_buffer_4_out;

  not not_1 (not_1_out, AccessType);
  assign controlled_buffer_1_out = AccessType ? S0_S7RW : 8'bz;  // Controlled_Buffer controlled_buffer_1
  assign controlled_buffer_2_out = not_1_out ? S0_S7RW : 8'bz;  // Controlled_Buffer controlled_buffer_2
  nand nand_1 (nand_1_out[0], controlled_buffer_2_out[7], controlled_buffer_2_out[7]);
  and and_1 (nand_1_out[1], controlled_buffer_2_out[7], controlled_buffer_2_out[7]);
  Demultiplexer #(.disabled("Z"), .select(4), .width(2)) demultiplexer_1 (
    .out0(demultiplexer_1_out0), .out1(demultiplexer_1_out1), .out2(demultiplexer_1_out2),
    .out3(demultiplexer_1_out3), .out4(demultiplexer_1_out4), .out5(demultiplexer_1_out5),
    .out6(demultiplexer_1_out6), .out7(demultiplexer_1_out7), .out8(demultiplexer_1_out8),
    .out9(demultiplexer_1_out9), .out10(demultiplexer_1_out10), .out11(demultiplexer_1_out11),
    .out12(demultiplexer_1_out12), .out13(demultiplexer_1_out13), .out14(demultiplexer_1_out14),
    .out15(demultiplexer_1_out15), .in(2'b01), .sel(controlled_buffer_1_out[3:0]));
  Demultiplexer #(.disabled("Z"), .select(4), .width(2)) demultiplexer_2 (
    .out0(demultiplexer_2_out0), .out1(demultiplexer_2_out1), .out2(demultiplexer_2_out2),
    .out3(demultiplexer_2_out3), .out4(demultiplexer_2_out4), .out5(demultiplexer_2_out5),
    .out6(demultiplexer_2_out6), .out7(demultiplexer_2_out7), .out8(demultiplexer_2_out8),
    .out9(demultiplexer_2_out9), .out10(demultiplexer_2_out10), .out11(demultiplexer_2_out11),
    .out12(demultiplexer_2_out12), .out13(demultiplexer_2_out13), .out14(demultiplexer_2_out14),
    .out15(demultiplexer_2_out15), .in(2'b10), .sel(controlled_buffer_1_out[7:4]));
  Demultiplexer #(.disabled("Z"), .select(4), .width(2)) demultiplexer_3 (
    .out0(demultiplexer_3_out0), .out1(demultiplexer_3_out1), .out2(demultiplexer_3_out2),
    .out3(demultiplexer_3_out3), .out4(demultiplexer_3_out4), .out5(demultiplexer_3_out5),
    .out6(demultiplexer_3_out6), .out7(demultiplexer_3_out7), .out8(demultiplexer_3_out8),
    .out9(demultiplexer_3_out9), .out10(demultiplexer_3_out10), .out11(demultiplexer_3_out11),
    .out12(demultiplexer_3_out12), .out13(demultiplexer_3_out13), .out14(demultiplexer_3_out14),
    .out15(demultiplexer_3_out15), .in(nand_1_out), .sel(controlled_buffer_2_out[3:0]));
  assign controlled_buffer_3_out = not_1_out ? {demultiplexer_3_out15, demultiplexer_3_out14, demultiplexer_3_out13, demultiplexer_3_out12, demultiplexer_3_out11, demultiplexer_3_out10, demultiplexer_3_out9, demultiplexer_3_out8, demultiplexer_3_out7, demultiplexer_3_out6, demultiplexer_3_out5, demultiplexer_3_out4, demultiplexer_3_out3, demultiplexer_3_out2, demultiplexer_3_out1, demultiplexer_3_out0} : 32'bz;  // Controlled_Buffer controlled_buffer_3
  assign controlled_buffer_4_out = AccessType ? {demultiplexer_2_out15, demultiplexer_2_out14, demultiplexer_2_out13, demultiplexer_2_out12, demultiplexer_2_out11, demultiplexer_2_out10, demultiplexer_2_out9, demultiplexer_2_out8, demultiplexer_2_out7, demultiplexer_2_out6, demultiplexer_2_out5, demultiplexer_2_out4, demultiplexer_2_out3, demultiplexer_2_out2, demultiplexer_2_out1, demultiplexer_2_out0, demultiplexer_1_out15, demultiplexer_1_out14, demultiplexer_1_out13, demultiplexer_1_out12, demultiplexer_1_out11, demultiplexer_1_out10, demultiplexer_1_out9, demultiplexer_1_out8, demultiplexer_1_out7, demultiplexer_1_out6, demultiplexer_1_out5, demultiplexer_1_out4, demultiplexer_1_out3, demultiplexer_1_out2, demultiplexer_1_out1, demultiplexer_1_out0} : 64'bz;  // Controlled_Buffer controlled_buffer_4
  assign or_1_out = controlled_buffer_4_out[31:0] | controlled_buffer_4_out[63:32];  // OR_Gate or_1, 32 bits wide
  assign {PC, INC_DEC, Stack, IE, MDR, MAR, RAM, Flag, L, H, E, D, C, B, temp, A} = RegAccess ? multiplexer_1_out : 32'bz;  // Controlled_Buffer controlled_buffer_5
  Multiplexer #(.width(32)) multiplexer_1 (
    .in0(or_1_out), .in1(controlled_buffer_3_out), .out(multiplexer_1_out), .sel(not_1_out));
endmodule

module INCDEC (
  input  [1:0] RW,
  input  [1:0] CLK_CLR,
  input  [7:0] BusIn,
  input  ID,
  output [7:0] BusOut
);

  wire adder_1_cout, and_1_out, and_2_out, and_3_out, or_1_out;
  wire [1:0] j_k_ff_1_q;
  wire [7:0] adder_1_out, multiplexer_1_out, multiplexer_2_out, multiplexer_3_out, multiplexer_4_out,
       register_1_q;

  Multiplexer #(.select(2), .width(8)) multiplexer_1 (
    .in0({8{1'b1}}), .in1({8{1'b1}}), .in2({8{1'b1}}), .in3({8{1'b0}}), .out(multiplexer_1_out),
    .sel(j_k_ff_1_q));
  Multiplexer #(.width(8)) multiplexer_2 (.in0({8{1'b0}}), .in1(8'h1), .out(multiplexer_2_out), .sel(j_k_ff_1_q[1]));
  Multiplexer #(.width(8)) multiplexer_3 (
    .in0(8'h1), .in1(multiplexer_2_out), .out(multiplexer_3_out), .sel(j_k_ff_1_q[0]));
  J_K_Flip_Flop j_k_ff_1 (
    .J(and_3_out), .clk(CLK_CLR[0]), .K(and_3_out), .Q(j_k_ff_1_q[0]), .reset(or_1_out));  // open: Qn, preset
  Multiplexer #(.width(8)) multiplexer_4 (
    .in0(multiplexer_3_out), .in1(multiplexer_1_out), .out(multiplexer_4_out), .sel(ID));
  or or_1 (or_1_out, CLK_CLR[1], and_2_out);
  and and_1 (and_1_out, RW[0], ~RW[1]);  // AND_Gate
  Register register_1 (.D(BusIn), .en(and_1_out), .Q(register_1_q), .clk(CLK_CLR[0]), .clr(CLK_CLR[1]));
  and and_2 (and_2_out, RW[1], RW[0]);
  Adder adder_1 (.a(register_1_q), .b(multiplexer_4_out), .out(adder_1_out), .cout(adder_1_cout));  // open: cin
  and and_3 (and_3_out, RW[1], ~RW[0]);  // AND_Gate
  assign BusOut = and_3_out ? adder_1_out : 8'bz;  // Controlled_Buffer controlled_buffer_1
  Register #(.width(1)) register_2 (
    .D(adder_1_cout), .Q(j_k_ff_1_q[1]), .clk(CLK_CLR[0]), .clr(CLK_CLR[1]));  // open: en
endmodule

module jump (
  input  ZF,
  input  [2:0] JMPData,
  input  SF,
  output JMP
);

  wire and_1_out, and_2_out, and_3_out, demultiplexer_1_out0, demultiplexer_1_out1, demultiplexer_1_out2,
       demultiplexer_1_out3, or_1_out;

  Demultiplexer #(.select(2)) demultiplexer_1 (
    .out0(demultiplexer_1_out0), .out1(demultiplexer_1_out1), .out2(demultiplexer_1_out2),
    .out3(demultiplexer_1_out3), .in(JMPData[0]), .sel(JMPData[2:1]));
  and and_1 (and_1_out, demultiplexer_1_out2, ~ZF);  // AND_Gate
  and and_2 (and_2_out, ZF, demultiplexer_1_out1);
  and and_3 (and_3_out, demultiplexer_1_out3, SF);
  or or_1 (or_1_out, and_1_out, and_2_out);
  or or_2 (JMP, demultiplexer_1_out0, or_1_out, and_3_out);
endmodule
